# Fritzing sketch newbody07202021 (saved by Fritzing 0.9.3b)

parts:
  S1 = Toggle Switch [package=THT]
  Bat1 = battery_holder_dual_18650 [part_number=TBH-18650-2A-P]
  Bat2 = battery_holder_dual_18650 [part_number=TBH-18650-2A-P]
  Part1 = Adafruit ADS1015 12Bit I2C ADC [part_number="Adafruit #1083"]
  U1 = Voltage Regulator [package=to220-adj]
  U2 = Voltage Regulator [package=to220-adj]
  Q1_GDS = Basic FET P-Channel [package="DPak [SMD]"]
  JP2 = Header 3 [package=screwterminal-3.5mm-3_lock.007s]
  Part2 = 16-Channel 12-bit PWM Servo Driver - I2C [part_number=PCA9685]
  Part3 = 16-Channel 12-bit PWM Servo Driver - I2C [part_number=PCA9685]
  F1 = FUSE [part_number="10A fuse" package=fuse_5mm]
  JP3 = Header 10 [package=1x10-2mm-smd]
  U6 = Voltage Regulator [package=to220-adj]
  Part4 = Mono 2.5W Class D Audio Amplifier - PAM8302
  Raspberry_Pi_1 = Raspberry Pi 4 [part_number=RPI-4-b]
  Part5 = Adafruit MAX9814 Electret Microphone Amplifier [part_number="Adafruit #1713"]
  Part7 = 2.4 Touchscreen TFT Breakout w:MicroSD
  J1 = Basic Servo [part_number="SG90 rotate"]  # not connected
  J2 = Basic Servo [part_number="SG90 tilt"]  # not connected
  JP4 = Header 10 [package=1x10-2mm-smd]
  JP5 = Header 10 [package=1x10-2mm-smd]
  SP1 = SPEAKER [package=pcb_mount_speaker]  # not connected
  BNO055 = 9-DOF Absolute Orientation IMU Fusion Breakout - BNO055
  JP6 = Header 10 [package=1x10-2mm-smd]
  R3 = Resistor [tolerance=±5% resistance=200k package=THT]
  R1 = Resistor [tolerance=±5% resistance=10k package=THT]
  R4 = Resistor [tolerance=±5% resistance=100k package=THT]

nets:
  N1: S1.COM, Q1_GDS.Gate, R1.Pin_0
  GND: S1.L2, Part1.GND, JP3.3, Part4.GND
  N2: Bat1.+#0, JP3.7
  N3: Bat1.+#1, Bat1.+#3
  N4: Bat1.+#2, JP2.1
  N5: Bat2.+#0, Bat2.+#2
  N6: Bat2.+#1, JP3.10
  N7: Bat2.+#3, JP2.3
  N8: Part1.AIN1, Part5.OUTPUT
  N9: Part1.AIN0, R3.Pin_0, R4.Pin_1
  N10: Part1.SDA, Part2.SDA, Part3.SDA, Raspberry_Pi_1.GPIO2, BNO055.SDA_5V
  N11: Part1.SCL, Part2.SCL, Part3.SCL, Raspberry_Pi_1.GPIO3, BNO055.SCL_5V
  N12: Part1.VDD, JP6.6
  N13: U1.ADJ, JP4.9
  N14: U1.IN, JP3.4
  N15: U1.OUT, Part2.PWRIN
  N16: U2.ADJ, JP4.10
  N17: U2.IN, JP3.9
  N18: U2.OUT, Part3.PWRIN
  N19: Q1_GDS.drain, R1.Pin_1
  N20: Q1_GDS.source, JP4.3
  N21: JP2.2, F1.1
  GND_2: Part2.GND, Part3.GND, JP3.5, JP3.6, JP3.8, BNO055.GND
  VCC: Part2.VCC, Part3.VCC, JP6.7
  GND_3: JP3.1, U6.IN, Part5.GND, Part7.GND
  N22: JP3.2, R4.Pin_0
  N23: U6.OUT, JP5.10
  N24: Part4.VCC, JP5.1
  N25: Raspberry_Pi_1.3v3, JP6.1
  N26: Raspberry_Pi_1.5V, JP5.2
  VDD: Part5.VDD, Part7.VIN, JP6.9
  N27: JP4.1, R3.Pin_1
  N28: BNO055.5.0V, JP6.10

notes:
  substitute for BEC
  O G I
  clean reg
  O G I
  clean +5V
  PI 3.3v
  Gain=60
  Gain-gnd=50db
  Gain-VDD=40db
  IM1,IM2,IM3 soldered for VDD 3.3v clk-SPIclk
  MOSI to spi MOSI
  CS to spichipsel
  D/C is data/command
  https://learn.adafruit.com/raspi-animated-gif-picture-frame
  GND
  BUS
  BATT MON
  BATT BUS
  ADC
  ADR-gnd 0x48 address
  S B E W G HHT K A A h h
  h i l r r i i h n n n e e
  o c b i i p p i e k k a a
  u e o s p B Sg e l l d d
  l p w t e p h e e t n
  d n l r f u o
  e d i o l r d
  r t l x n
  Right side 0x40
  S B E W G HHT K A A h h
  h i l r r i i h n n n e e
  o c b i i p p i e k k a a
  u e o s p B Sg e l l d d
  l p w t e p h e e t n
  d n l r f u o
  e d i o l r d
  r t l x n
  Left side 0x41
  Raspberry PI 4 8GB
  w/256GiB sdcard ubuntu +

custom parts:
  battery_holder_dual_18650: TBH-18650-2A-P dual 18650 battery holder.
  Adafruit ADS1015 12Bit I2C ADC: For microcontrollers without an analog-to-digital converter or when you want a higher-precision ADC, the ADS1015 provides 12-bit precision at 3300 samples/second over I2C. The chip can be configured as 4 single-ended input channels, or two differential channels. As a nice bonus, it even includes a programmable gain amplifier, up to x16, to help boost up smaller single/differential signals to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
  16-Channel 12-bit PWM Servo Driver - I2C: You want to make a cool robot, maybe a hexapod walker, or maybe just a piece of art with a lot of moving parts. Or maybe you want to drive a lot of LEDs with precise PWM output. Using only two pins, control 16 free-running PWM outputs! You can even chain up 62 breakouts to control up to 992 PWM outputs.
  Mono 2.5W Class D Audio Amplifier - PAM8302: A super small but powerful mono amplifier able to deliver up to 2.5 Watts into 4-8 ohm impedance speakers. Inside the miniature chip is a class D controller, able to run from 2.0V-5.5VDC. Since the amp is a class D, its very efficient (over 90% efficient when driving an 8Ω speaker at over half a Watt) - making it perfect for portable and battery-powered projects.
  Raspberry Pi 4: The RPi4, a faster version of the awesome Raspberry Pi 2 B ARM Board with 40 pin gpio. Ready for special Raspberry Pi B+ and RPi2 Hat (Hardware attached (on) top)
  Adafruit MAX9814 Electret Microphone Amplifier: Add an ear to your project with this well-designed electret microphone amplifier with AGC. This fully assembled and tested board comes with a 20-20KHz electret microphone soldered on. For the amplification, we use the Maxim MAX9814, a specialty chip that is designed for amplifying electret microphones in situations where the loudness of the audio isn't predictable. This fancy microphone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
  2.4 Touchscreen TFT Breakout w:MicroSD: Add some jazz & pizzazz to your project with a color touchscreen LCD. This TFT display is 2.4" diagonal with a bright (4 white-LED) backlight and it's colorful! 240x320 pixels with individual RGB pixel control, this has way more resolution than a black and white 128x64 display. As a bonus, this display has a resistive touchscreen attached to it already, so you can detect finger presses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
  9-DOF Absolute Orientation IMU Fusion Breakout - BNO055: A MEMS accelerometer, magnetometer and gyroscope on a single die with a high speed ARM Cortex-M0 based processor to digest all the sensor data, abstract the sensor fusion and real time requirements away, and spit out data you can use in quaternions, Euler angles or vectors.
